# Fritzing sketch main (saved by Fritzing 0.9.3b)
breadboards: 1

parts:
  Part1 = Bluetooth HC-06
  Part2 = Arduino Uno (Rev3) - ICSP
  LED1 = smd LED [color="Red (633nm)" package="1206 [SMD]"]
  R1 = Resistor [tolerance=±5% resistance=220 package="0402 [SMD]"]

nets:
  N1: Part1.RXD, Part2.D1/TX
  N2: Part1.TXD, Part2.D0/RX
  GND: Part1.GND, Part2.GND, R1.Pin_1
  VCC: Part1.VCC, Part2.5V
  N3: Part2.D13/SCK, LED1.anode
  N4: LED1.cathode, R1.Pin_0

// code stored in the sketch: arduino.ino
int led = 13;

void setup () {
	Serial.begin(9600);
	pinMode(led, OUTPUT);
}

void loop () {
	delay(800);
	digitalWrite(led, HIGH);
	delay(800);
	digitalWrite(led, LOW);
}
